# Fritzing sketch schematic (saved by Fritzing 0.9.3b)

parts:
  Part2 = 24 NeoPixel Ring [part_number=1586]  # not connected
  A1 = Esp32-c3 super mini
  Grove1 = TM1637 7segment 4digit display
  J1 = Buzzer  # not connected
  Part3 = SRF05 Ultrasonic Rangefinder
  R1 = Resistor [tolerance=±5% resistance=220 package="0805 [SMD]"]

nets:
  N1: A1.Pin_4, Grove1.CLK
  N2: A1.Pin_5, Grove1.DIO
  N3: A1.Pin_10, Part3.Echo
  N4: A1.Pin_11, Part3.Trig
  N5: A1.Pin_13, R1.Pin_1

custom parts:
  24 NeoPixel Ring: 24 ultra bright smart LED NeoPixels are arranged in a circle with 2.6" (66mm) outer diameter. The rings are 'chainable' - connect the output pin of one to the input pin of another. Use only one microcontroller pin to control as many as you can chain together! Each LED is addressable as the driver chip is inside the LED. Each one has ~18mA constant current drive so the color will be very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
  Esp32-c3 super mini: ESP32-C3 Development Board ESP32 SuperMini Development Board ESP32 Development Board WiFi Bluetooth.
  Buzzer: Fixed frequency buzzer
